# Fritzing sketch Infrared (saved by Fritzing 0.9.3b)
breadboards: 1

parts:
  IR1 = TSOP312.., 314.. [package=THT]
  LED1 = LED - 5mm [color="Red (633nm)" package="5 mm [THT]"]
  LED2 = LED - 5mm [color="Red (633nm)" package="5 mm [THT]"]
  LED3 = LED - 5mm [color="Red (633nm)" package="5 mm [THT]"]
  Part1 = Arduino Uno (Rev3)
  R1 = Resistor [tolerance=±5% resistance=220 package=THT]
  R2 = Resistor [tolerance=±5% resistance=220 package=THT]
  R3 = Resistor [tolerance=±5% resistance=220 package=THT]

nets:
  N1: IR1.GND, Part1.D3_PWM
  N2: IR1.Vs, Part1.GND
  N3: IR1.Data, Part1.3V3
  N4: LED1.cathode, LED2.cathode, LED3.cathode, LED3.anode
  N5: LED1.anode, R1.Pin_0
  N6: LED2.anode, R2.Pin_0
  N7: Part1.D4, R1.Pin_1
  N8: Part1.D5_PWM, R2.Pin_1
  N9: Part1.D6_PWM, R3.Pin_1
